// Logisim project adder.circ as structural Verilog: 2 circuits, main circuit ripple adder/subtractor
module full_adder (
  input  Cin,
  input  sub,
  input  A,
  input  B,
  output result,
  output ovf
);

  wire and_1_out, and_2_out, multiplexer_1_out, not_1_out, xor_1_out;

  not not_1 (not_1_out, B);
  Multiplexer multiplexer_1 (.in0(B), .in1(not_1_out), .out(multiplexer_1_out), .sel(sub));  // open: en
  and and_1 (and_1_out, A, multiplexer_1_out);
  xor xor_1 (xor_1_out, A, multiplexer_1_out);
  xor xor_2 (result, Cin, xor_1_out);
  and and_2 (and_2_out, Cin, xor_1_out);
  or or_1 (ovf, and_2_out, and_1_out);
endmodule

module ripple_adder_subtractor (
  input  sub,
  input  [15:0] A,
  input  [15:0] B,
  output [15:0] result,
  output ovf
);

  wire full_adder_1_ovf, full_adder_2_ovf, full_adder_3_ovf, full_adder_4_ovf, full_adder_5_ovf,
       full_adder_6_ovf, full_adder_7_ovf, full_adder_8_ovf, full_adder_9_ovf, full_adder_10_ovf,
       full_adder_11_ovf, full_adder_12_ovf, full_adder_13_ovf, full_adder_14_ovf, full_adder_15_ovf,
       full_adder_16_ovf;

  full_adder full_adder_1 (.Cin(sub), .sub(sub), .A(A[0]), .B(B[0]), .result(result[0]), .ovf(full_adder_1_ovf));
  full_adder full_adder_2 (
    .Cin(full_adder_1_ovf), .sub(sub), .A(A[1]), .B(B[1]), .result(result[1]), .ovf(full_adder_2_ovf));
  full_adder full_adder_3 (
    .Cin(full_adder_2_ovf), .sub(B[2]), .A(A[2]), .B(sub), .result(result[2]), .ovf(full_adder_3_ovf));
  full_adder full_adder_4 (
    .Cin(full_adder_3_ovf), .sub(sub), .A(A[3]), .B(B[3]), .result(result[3]), .ovf(full_adder_4_ovf));
  full_adder full_adder_5 (
    .Cin(full_adder_4_ovf), .sub(sub), .A(A[4]), .B(B[4]), .result(result[4]), .ovf(full_adder_5_ovf));
  full_adder full_adder_6 (
    .Cin(full_adder_5_ovf), .sub(sub), .A(A[5]), .B(B[5]), .result(result[5]), .ovf(full_adder_6_ovf));
  full_adder full_adder_7 (
    .Cin(full_adder_6_ovf), .sub(sub), .A(A[6]), .B(B[6]), .result(result[6]), .ovf(full_adder_7_ovf));
  full_adder full_adder_8 (
    .Cin(full_adder_7_ovf), .sub(sub), .A(A[7]), .B(B[7]), .result(result[7]), .ovf(full_adder_8_ovf));
  full_adder full_adder_9 (
    .Cin(full_adder_8_ovf), .sub(sub), .A(A[8]), .B(B[8]), .result(result[8]), .ovf(full_adder_9_ovf));
  full_adder full_adder_10 (
    .Cin(full_adder_9_ovf), .sub(sub), .A(A[9]), .B(B[9]), .result(result[9]), .ovf(full_adder_10_ovf));
  full_adder full_adder_11 (
    .Cin(full_adder_10_ovf), .sub(sub), .A(A[10]), .B(B[10]), .result(result[10]), .ovf(full_adder_11_ovf));
  full_adder full_adder_12 (
    .Cin(full_adder_11_ovf), .sub(sub), .A(A[11]), .B(B[11]), .result(result[11]), .ovf(full_adder_12_ovf));
  full_adder full_adder_13 (
    .Cin(full_adder_12_ovf), .sub(sub), .A(A[12]), .B(B[12]), .result(result[12]), .ovf(full_adder_13_ovf));
  full_adder full_adder_14 (
    .Cin(full_adder_13_ovf), .sub(sub), .A(A[13]), .B(B[13]), .result(result[13]), .ovf(full_adder_14_ovf));
  full_adder full_adder_15 (
    .Cin(full_adder_14_ovf), .sub(sub), .A(A[14]), .B(B[14]), .result(result[14]), .ovf(full_adder_15_ovf));
  full_adder full_adder_16 (
    .Cin(full_adder_15_ovf), .sub(sub), .A(A[15]), .B(B[15]), .result(result[15]), .ovf(full_adder_16_ovf));
  xor xor_1 (ovf, full_adder_16_ovf, full_adder_15_ovf);
endmodule
