// Logisim project fsm.circ as structural Verilog: 1 circuit, main circuit main
module main (
  input  in1,
  input  in2,
  output out1,
  output out2
);

  wire and_1_out, and_2_out, and_3_out, and_4_out, and_5_out, and_6_out, and_7_out, and_8_out, and_9_out,
       and_10_out, and_11_out, and_12_out, clock_1_out, CS0, CS1, not_1_out, not_2_out, not_3_out, not_4_out,
       not_5_out, not_6_out, not_7_out, not_8_out, not_9_out, not_10_out, not_11_out, not_12_out, not_13_out,
       not_14_out, not_15_out, not_16_out, not_17_out, not_18_out, not_19_out, not_20_out, not_21_out,
       or_1_out, or_2_out;

  not not_1 (not_1_out, in2);
  not not_2 (not_2_out, CS0);
  not not_3 (not_3_out, CS1);
  not not_4 (not_4_out, CS1);
  not not_5 (not_5_out, in1);
  not not_6 (not_6_out, CS1);
  not not_7 (not_7_out, CS0);
  not not_8 (not_8_out, in2);
  not not_9 (not_9_out, CS0);
  not not_10 (not_10_out, CS1);
  not not_11 (not_11_out, in1);
  not not_12 (not_12_out, CS1);
  not not_13 (not_13_out, in1);
  not not_14 (not_14_out, in2);
  not not_15 (not_15_out, CS0);
  not not_16 (not_16_out, in1);
  not not_17 (not_17_out, in2);
  not not_18 (not_18_out, CS0);
  not not_19 (not_19_out, CS1);
  and and_1 (and_1_out, not_5_out, in2, not_6_out, not_7_out);
  and and_2 (and_2_out, in1, not_8_out, not_9_out, not_10_out);
  not not_20 (not_20_out, CS0);
  and and_3 (and_3_out, not_11_out, in2, CS0, CS1);
  and and_4 (and_4_out, in1, not_1_out, CS0, CS1);
  and and_5 (and_5_out, CS0, not_12_out);
  and and_6 (and_6_out, not_13_out, in2, not_2_out, CS1);
  and and_7 (and_7_out, not_16_out, in2, CS0, not_3_out);
  and and_8 (and_8_out, in1, not_17_out, CS0, not_4_out);
  and and_9 (and_9_out, not_18_out, not_19_out);
  and and_10 (and_10_out, CS0, CS1);
  and and_11 (and_11_out, not_20_out, CS1);
  and and_12 (and_12_out, in1, not_14_out, not_15_out, CS1);
  or or_1 (or_1_out, and_1_out, and_2_out, and_11_out, and_3_out, and_4_out, and_5_out);
  or or_2 (or_2_out, and_6_out, and_12_out, and_7_out, and_8_out, and_9_out, and_10_out);
  Clock clock_1 (.out(clock_1_out));
  D_Flip_Flop u_CS0 (.clk(clock_1_out), .D(or_1_out), .Q(CS0));  // open: Qn, preset, en, reset
  D_Flip_Flop u_CS1 (.clk(clock_1_out), .D(or_2_out), .Q(CS1));  // open: Qn, preset, en, reset
  and and_13 (out1, CS0, not_21_out);
  not not_21 (not_21_out, CS1);
  and and_14 (out2, CS0, CS1);
endmodule
