// Logisim project hw4.circ as structural Verilog: 7 circuits, main circuit CPU
module RegisterFile (
  input  [2:0] writeReg,
  input  [2:0] readReg1,
  input  [2:0] readReg2,
  input  writeEnable,
  input  reset,
  input  [15:0] writeData,
  input  in_7,
  output [15:0] readData1,
  output [15:0] readData2
);

  wire and_1_out, and_2_out, and_3_out, and_4_out, and_5_out, and_6_out, and_7_out, and_8_out,
       decoder_1_out0, decoder_1_out1, decoder_1_out2, decoder_1_out3, decoder_1_out4, decoder_1_out5,
       decoder_1_out6, decoder_1_out7;
  wire [15:0] register_1_q, register_2_q, register_3_q, register_4_q, register_5_q, register_6_q,
       register_7_q, register_8_q;

  Decoder #(.select(3), .enable("false")) decoder_1 (
    .out0(decoder_1_out0), .out1(decoder_1_out1), .out2(decoder_1_out2), .out3(decoder_1_out3),
    .out4(decoder_1_out4), .out5(decoder_1_out5), .out6(decoder_1_out6), .out7(decoder_1_out7), .sel(writeReg));
  and and_1 (and_1_out, decoder_1_out0, 1'b0);
  and and_2 (and_2_out, decoder_1_out1, writeEnable);
  and and_3 (and_3_out, decoder_1_out2, writeEnable);
  and and_4 (and_4_out, decoder_1_out3, writeEnable);
  and and_5 (and_5_out, decoder_1_out4, writeEnable);
  and and_6 (and_6_out, decoder_1_out5, writeEnable);
  and and_7 (and_7_out, decoder_1_out6, writeEnable);
  and and_8 (and_8_out, decoder_1_out7, writeEnable);
  // Probe on register_1_q
  Register #(.width(16), .trigger("falling")) register_1 (
    .D(writeData), .en(and_1_out), .Q(register_1_q), .clk(in_7), .clr(reset));
  Register #(.width(16), .trigger("falling")) register_2 (
    .D(writeData), .en(and_2_out), .Q(register_2_q), .clk(in_7), .clr(reset));
  Register #(.width(16), .trigger("falling")) register_3 (
    .D(writeData), .en(and_3_out), .Q(register_3_q), .clk(in_7), .clr(reset));
  Register #(.width(16), .trigger("falling")) register_4 (
    .D(writeData), .en(and_4_out), .Q(register_4_q), .clk(in_7), .clr(reset));
  Register #(.width(16), .trigger("falling")) register_5 (
    .D(writeData), .en(and_5_out), .Q(register_5_q), .clk(in_7), .clr(reset));
  Register #(.width(16), .trigger("falling")) register_6 (
    .D(writeData), .en(and_6_out), .Q(register_6_q), .clk(in_7), .clr(reset));
  Register #(.width(16), .trigger("falling")) register_7 (
    .D(writeData), .en(and_7_out), .Q(register_7_q), .clk(in_7), .clr(reset));
  Register #(.width(16), .trigger("falling")) register_8 (
    .D(writeData), .en(and_8_out), .Q(register_8_q), .clk(in_7), .clr(reset));
  // Probe on register_2_q
  // Probe on register_7_q
  // Probe on register_8_q
  Multiplexer #(.select(3), .width(16), .enable("false")) multiplexer_1 (
    .in0(register_1_q), .in1(register_2_q), .in2(register_3_q), .in3(register_4_q), .in4(register_5_q),
    .in5(register_6_q), .in6(register_7_q), .in7(register_8_q), .out(readData1), .sel(readReg1));
  // Probe on register_3_q
  // Probe on register_4_q
  // Probe on register_5_q
  // Probe on register_6_q
  Multiplexer #(.select(3), .width(16), .enable("false")) multiplexer_2 (
    .in0(register_1_q), .in1(register_2_q), .in2(register_3_q), .in3(register_4_q), .in4(register_5_q),
    .in5(register_6_q), .in6(register_7_q), .in7(register_8_q), .out(readData2), .sel(readReg2));

  // Other names for the same wires on the sheet: clk = in_7; data[15:0] = writeData; rs[2:0] = readReg1;
  //   rt[2:0] = readReg2; we = writeEnable
endmodule

module CPU (
  input  reset
);

  wire addi, and_1_out, b_en, b_sel, blt, bne, clk_out, j_en, jr, keyboard_1_avail, keyen, multiplexer_4_out,
       not_1_out, RAMwe, RF_en, TTYen;
  wire [1:0] wdata, wreg;
  wire [2:0] ALUop, multiplexer_5_out, rd, rs, rt, sh;
  wire [3:0] op;
  wire [5:0] im;
  wire [6:0] helper2_1_out_2, keyboard_1_data;
  wire [11:0] ad;
  wire [15:0] adder_1_out, adder_2_out, ALU_output, bit_extender_1_out, bit_extender_2_out,
       bit_extender_3_out, helper_1_l, multiplexer_1_out, multiplexer_2_out, multiplexer_3_out,
       multiplexer_6_out, multiplexer_7_out, multiplexer_8_out, ram_1_data, register_1_q,
       RegisterFile_readdata1, RegisterFile_readdata2, rom_1_data;

  helper helper_1 (.address(ad), .PC_input(register_1_q), .L(helper_1_l));
  Multiplexer #(.width(16), .enable("false")) multiplexer_1 (
    .in0(adder_2_out), .in1(adder_1_out), .out(multiplexer_1_out), .sel(and_1_out));
  Multiplexer #(.width(16), .enable("false")) multiplexer_2 (
    .in0(helper_1_l), .in1(RegisterFile_readdata1), .out(multiplexer_2_out), .sel(jr));
  and and_1 (and_1_out, b_en, multiplexer_4_out);
  control CONTROL (
    .opcode(op), .RE_enable(RF_en), .branch_enable(b_en), .branch_instruct_chooser(b_sel),
    .j_jr_jal_enable(j_en), .jr_specific_enable(jr), .write_data_selector(wdata),
    .register_for_written_data_selector(wreg), .ALUop(ALUop), .addi_enable(addi), .RAM_write_enable(RAMwe),
    .keyboard_enable(keyen), .TTY_enable(TTYen));
  Multiplexer #(.width(16), .enable("false")) multiplexer_3 (
    .in0(multiplexer_1_out), .in1(multiplexer_2_out), .out(multiplexer_3_out), .sel(j_en));
  Multiplexer #(.enable("false")) multiplexer_4 (.in0(bne), .in1(blt), .out(multiplexer_4_out), .sel(b_sel));
  Clock clk (.out(clk_out));
  Adder #(.width(16)) adder_1 (.a(bit_extender_1_out), .b(adder_2_out), .out(adder_1_out));  // open: cin, cout
  Register #(.width(16)) register_1 (.D(multiplexer_3_out), .en(1'b1), .Q(register_1_q), .clk(clk_out), .clr(reset));
  Adder #(.width(16)) adder_2 (.a(register_1_q), .b(16'h1), .out(adder_2_out));  // open: cin, cout
  ROM #(.addrWidth(16), .dataWidth(16)) rom_1 (.addr(register_1_q), .data(rom_1_data));  // open: sel
  Keyboard keyboard_1 (.clk(clk_out), .re(keyen), .clr(reset), .avail(keyboard_1_avail), .data(keyboard_1_data));
  assign bit_extender_1_out = {{10{im[5]}}, im};  // Bit_Extender bit_extender_1
  instruction_decoder inst_decoder (
    .instruction(rom_1_data), .address(ad), .immediate(im), .shamt(sh), .rd(rd), .rt(rt), .rs(rs),
    .op_code(op));
  Multiplexer #(.select(2), .width(3), .enable("false")) multiplexer_5 (
    .in0(rd), .in1(rt), .in2(3'b111), .out(multiplexer_5_out), .sel(wreg));  // open: in3
  Multiplexer #(.width(16), .enable("false")) multiplexer_6 (
    .in0(16'h80), .in1(bit_extender_2_out), .out(multiplexer_6_out), .sel(keyboard_1_avail));
  assign bit_extender_2_out = {{9{1'b0}}, keyboard_1_data};  // Bit_Extender bit_extender_2
  RegisterFile RegisterFile (
    .writeReg(multiplexer_5_out), .readReg1(rs), .readReg2(rt), .writeEnable(RF_en), .reset(reset),
    .writeData(multiplexer_7_out), .in_7(clk_out), .readData1(RegisterFile_readdata1),
    .readData2(RegisterFile_readdata2));
  Multiplexer #(.select(2), .width(16), .enable("false")) multiplexer_7 (
    .in0(ALU_output), .in1(ram_1_data), .in2(adder_2_out), .in3(multiplexer_6_out), .out(multiplexer_7_out),
    .sel(wdata));
  assign bit_extender_3_out = {{10{im[5]}}, im};  // Bit_Extender bit_extender_3
  Multiplexer #(.width(16), .enable("false")) multiplexer_8 (
    .in0(RegisterFile_readdata2), .in1(bit_extender_3_out), .out(multiplexer_8_out), .sel(addi));
  not not_1 (not_1_out, clk_out);
  ALU ALU (
    .op1(RegisterFile_readdata1), .op2(multiplexer_8_out), .selector(ALUop), .shamt(sh), .bne(bne),
    .blt(blt), .\output (ALU_output));
  RAM #(.addrWidth(16), .dataWidth(16), .bus("separate")) ram_1 (
    .addr(ALU_output), .din(RegisterFile_readdata2), .data(ram_1_data), .str(RAMwe), .clk(not_1_out));  // open: sel, ld, clr
  helper2 helper2_1 (.in_1(RegisterFile_readdata1), .out_2(helper2_1_out_2));
  TTY #(.rows(13), .cols(80), .trigger("falling")) tty_1 (
    .data(helper2_1_out_2), .clk(clk_out), .we(TTYen), .clr(reset));
endmodule

module instruction_decoder (
  input  [15:0] instruction,
  output [11:0] address,
  output [5:0] immediate,
  output [2:0] shamt,
  output [2:0] rd,
  output [2:0] rt,
  output [2:0] rs,
  output [3:0] op_code
);


  assign address = instruction[11:0];
  assign immediate = instruction[5:0];
  assign op_code = instruction[15:12];
  assign rd = instruction[5:3];
  assign rs = instruction[11:9];
  assign rt = instruction[8:6];
  assign shamt = instruction[2:0];
endmodule

module ALU (
  input  [15:0] op1,
  input  [15:0] op2,
  input  [2:0] selector,
  input  [2:0] shamt,
  output bne,
  output blt,
  output [15:0] \output 
);

  wire comparator_1_eq;
  wire [3:0] bit_extender_1_out;
  wire [15:0] adder_1_out, not_1_out, shifter_1_out, shifter_2_out, subtractor_1_out, xor_1_out;

  assign bit_extender_1_out = {{1{1'b0}}, shamt};  // Bit_Extender bit_extender_1
  Subtractor #(.width(16)) subtractor_1 (.a(op1), .b(op2), .out(subtractor_1_out));  // open: bin, bout
  assign xor_1_out = op1 ^ op2;  // XOR_Gate xor_1, 16 bits wide
  Adder #(.width(16)) adder_1 (.a(op1), .b(op2), .out(adder_1_out));  // open: cin, cout
  Shifter #(.width(16), .shift("ar")) shifter_1 (.in(op1), .\dist (bit_extender_1_out), .out(shifter_1_out));
  Shifter #(.width(16)) shifter_2 (.in(op1), .\dist (bit_extender_1_out), .out(shifter_2_out));
  Comparator #(.width(16)) comparator_1 (.a(op1), .b(op2), .eq(comparator_1_eq), .lt(blt));  // open: gt
  assign not_1_out = ~op1;  // NOT_Gate not_1, 16 bits wide
  not not_2 (bne, comparator_1_eq);
  Multiplexer #(.select(3), .width(16), .enable("false")) multiplexer_1 (
    .in0(adder_1_out), .in1(subtractor_1_out), .in2(not_1_out), .in3(xor_1_out), .in4(shifter_1_out),
    .in5(shifter_2_out), .out(\output ), .sel(selector));  // open: in6, in7

  // Other names for the same wires on the sheet: s[2:0] = selector
endmodule

module helper (
  input  [11:0] address,
  input  [15:0] PC_input,
  output [15:0] L
);


  assign L = {PC_input[15:12], address};
endmodule

module helper2 (
  input  [15:0] in_1,
  output [6:0] out_2
);


  assign out_2 = in_1[6:0];
endmodule

module control (
  input  [3:0] opcode,
  output RE_enable,
  output branch_enable,
  output branch_instruct_chooser,
  output j_jr_jal_enable,
  output jr_specific_enable,
  output [1:0] write_data_selector,
  output [1:0] register_for_written_data_selector,
  output [2:0] ALUop,
  output addi_enable,
  output RAM_write_enable,
  output keyboard_enable,
  output TTY_enable
);

  wire decoder_1_out0, decoder_1_out1, decoder_1_out2, decoder_1_out3, decoder_1_out4, decoder_1_out5,
       decoder_1_out6, decoder_1_out7, decoder_1_out9, decoder_1_out12;

  Decoder #(.select(4), .enable("false")) decoder_1 (
    .out0(decoder_1_out0), .out1(decoder_1_out1), .out2(decoder_1_out2), .out3(decoder_1_out3),
    .out4(decoder_1_out4), .out5(decoder_1_out5), .out6(decoder_1_out6), .out7(decoder_1_out7),
    .out8(RAM_write_enable), .out9(decoder_1_out9), .out10(register_for_written_data_selector[1]),
    .out11(jr_specific_enable), .out12(decoder_1_out12), .out13(branch_instruct_chooser),
    .out14(keyboard_enable), .out15(TTY_enable), .sel(opcode));
  or or_1 (write_data_selector[0], decoder_1_out7, keyboard_enable);
  or or_2 (write_data_selector[1], register_for_written_data_selector[1], keyboard_enable);
  or or_3 (register_for_written_data_selector[0], decoder_1_out7, decoder_1_out2);
  or or_4 (ALUop[0], decoder_1_out6, decoder_1_out4, decoder_1_out1);
  or or_5 (ALUop[1], decoder_1_out0, decoder_1_out1);
  or or_6 (ALUop[2], decoder_1_out5, decoder_1_out6);
  or or_7 (branch_enable, decoder_1_out12, branch_instruct_chooser);
  or or_8 (j_jr_jal_enable, jr_specific_enable, register_for_written_data_selector[1], decoder_1_out9);
  or or_9 (RE_enable, decoder_1_out0, decoder_1_out1, decoder_1_out2, decoder_1_out3, decoder_1_out4, decoder_1_out5, decoder_1_out6, decoder_1_out7, register_for_written_data_selector[1], keyboard_enable);
  or or_10 (addi_enable, decoder_1_out2, decoder_1_out7, RAM_write_enable);
endmodule
